# Fritzing sketch Aquacontrol Schematic (saved by Fritzing 0.8.3b)
circuit board: 6.9958cm x 5.56284cm
breadboards: 3

parts:
  Arduino_Uno = Arduino Uno (Rev3)
  J1 = screw terminal, 3 pins [part_number=DS18S20]
  R2 = TRIMPOT [part_number="10k Ohm" package=trimpot_pth_s3_lock]
  IC1 = DS1307 [part_number=2 package=THT]
  BAT1 = Battery Holders [package=battcom_20mm_pth]
  XTAL1 = CRYSTAL - kHz [frequency="32 kHz"]
  J3 = female pin header, 16 pins [form="♀ (female)" part_number=LCD-Display]
  R3 = Resistor [tolerance=±5% resistance=4.7k package=THT]
  Q1 = PNP-Transistor [part_number=2N2222 package="TO92 [THT]"]
  J4 = female pin header, 6 pins [form="♀ (female)" part_number="Switch 1 - 5"]
  R4 = Resistor [tolerance=±5% resistance=330 package=THT]
  R5 = Resistor [tolerance=±5% resistance=620 package=THT]
  R6 = Resistor [tolerance=±5% resistance=1k package=THT]
  R7 = Resistor [tolerance=±5% resistance=3.3k package=THT]
  R8 = Resistor [tolerance=±1% resistance=1.5k package=THT]
  IC2 = MCP23017 I2C I/O Expander
  J5 = female pin header, 10 pins [form="♀ (female)" part_number="Port B"]
  J6 = female pin header, 10 pins [form="♀ (female)" part_number="Port A"]
  J2 = screw terminal, 3 pins [part_number=DS18S20]
  R9 = Resistor [tolerance=±1% resistance=4.7k package=THT]
  R10 = Resistor [tolerance=±1% resistance=4.7k package=THT]
  R11 = Resistor [tolerance=±1% resistance=4.7k package=THT]

nets:
  A0: Arduino_Uno.A0, J4.pin2, R4.Pin_0, R8.Pin_1
  SDA: Arduino_Uno.A4/SDA, IC1.SDA_-_I2C_Data, IC2.SDA, R9.Pin_1
  SCL: Arduino_Uno.A5/SCL, IC1.SCL_-_I2C_Clock, IC2.SCL, R10.Pin_1
  5V: Arduino_Uno.5V, J1.pin3, R2.CW, IC1.+V, J3.pin2, J3.pin15, R3.Pin_0, R8.Pin_0, IC2.VDD, J5.pin2, J6.pin2, J2.pin3, R9.Pin_0, R10.Pin_0, R11.Pin_1
  GND: Arduino_Uno.GND, J1.pin1, R2.CCW, IC1.0V, BAT1.-, J3.pin1, J3.pin5, Q1.E, J4.pin1, IC2.VSS, IC2.A0, IC2.A1, IC2.A2, J5.pin1, J6.pin1, J2.pin1
  N1: Arduino_Uno.D8, J3.pin4
  N2: Arduino_Uno.D9_PWM, J3.pin6
  N3: Arduino_Uno.D10_PWM/SS, R3.Pin_1, Q1.B
  1-Wire: Arduino_Uno.D2, J1.pin2, J2.pin2, R11.Pin_0
  N4: Arduino_Uno.D4, J3.pin11
  N5: Arduino_Uno.D5_PWM, J3.pin12
  N6: Arduino_Uno.D6_PWM, J3.pin13
  N7: Arduino_Uno.D7, J3.pin14
  RESET: Arduino_Uno.RESET, IC2.RESET
  N8: R2.WIPER, J3.pin3
  N9: IC1.X1_-_Crystal, XTAL1.pin_1
  N10: IC1.X2_-_Crystal, XTAL1.pin_0
  N11: IC1.Vbat_-_Backup_Supply, BAT1.+
  N12: J3.pin16, Q1.C
  N13: J4.pin3, R4.Pin_1, R5.Pin_0
  N14: J4.pin4, R5.Pin_1, R6.Pin_0
  N15: J4.pin5, R6.Pin_1, R7.Pin_1
  N16: J4.pin6, R7.Pin_0
  N17: IC2.GPB0, J5.pin3
  N18: IC2.GPB1, J5.pin4
  N19: IC2.GPB2, J5.pin5
  N20: IC2.GPB3, J5.pin6
  N21: IC2.GPB4, J5.pin7
  N22: IC2.GPB5, J5.pin8
  N23: IC2.GPB6, J5.pin9
  N24: IC2.GPB7, J5.pin10
  N25: IC2.GPA0, J6.pin3
  N26: IC2.GPA1, J6.pin4
  N27: IC2.GPA2, J6.pin5
  N28: IC2.GPA3, J6.pin6
  N29: IC2.GPA4, J6.pin7
  N30: IC2.GPA5, J6.pin8
  N31: IC2.GPA6, J6.pin9
  N32: IC2.GPA7, J6.pin10

notes:
  RTC 1307
  I2C Port-Extender
  Taster
  Relais
  RTC
  Temp
  LCD
  Aquacontrol V1.0
  1

custom parts:
  MCP23017 I2C I/O Expander: MCP23017 I2C 16-Channel I/O Expander
